// Logisim project control_logic.circ as structural Verilog: 1 circuit, main circuit control_logic
module control_logic (
  input  [31:0] inst,
  input  BrEq,
  input  BrLt,
  output PCSel,
  output RegWEn,
  output [2:0] ImmSel,
  output BrUn,
  output ASel,
  output BSel,
  output [3:0] ALUSel,
  output MemRW,
  output [1:0] WBSel,
  output CSRSel,
  output CSRWen,
  output [1:0] loadSel
);

  wire and_1_out, and_2_out, and_3_out, and_4_out, and_5_out, and_6_out, and_13_out, b, comparator_3_eq,
       comparator_4_eq, comparator_10_eq, comparator_11_eq, comparator_12_eq, comparator_13_eq,
       comparator_14_eq, comparator_15_eq, comparator_16_eq, comparator_17_eq, comparator_19_eq,
       comparator_20_eq, comparator_21_eq, comparator_22_eq, comparator_23_eq, comparator_25_eq,
       comparator_26_eq, comparator_27_eq, comparator_28_eq, h, hasFunc7, load, multiplexer_1_out, not_1_out,
       not_2_out, not_3_out, or_3_out, or_4_out, or_7_out, or_9_out, or_12_out, typeAuipc, typeB, typeCsrrw,
       typeCsrrwi, typeI, typeJ, typeJalr, typeLui, typeR, typeU, useALU, w;
  wire [1:0] multiplexer_14_out, multiplexer_15_out, multiplexer_16_out;
  wire [2:0] ALUSel0, multiplexer_2_out, multiplexer_3_out, multiplexer_7_out, multiplexer_9_out;
  wire [3:0] multiplexer_4_out, multiplexer_5_out, multiplexer_6_out, multiplexer_8_out, multiplexer_10_out;

  Comparator #(.width(7)) comparator_1 (.a(inst[6:0]), .b(7'b0110011), .eq(typeR));  // open: gt, lt
  Comparator #(.width(7)) comparator_2 (.a(inst[6:0]), .b(7'b0000011), .eq(load));  // open: gt, lt
  Comparator #(.width(7)) comparator_3 (.a(inst[6:0]), .b(7'b1100111), .eq(comparator_3_eq));  // open: gt, lt
  Comparator #(.width(7)) comparator_4 (.a(inst[6:0]), .b(7'b0010011), .eq(comparator_4_eq));  // open: gt, lt
  Comparator #(.width(7)) comparator_5 (.a(inst[6:0]), .b(7'b0100011), .eq(MemRW));  // open: gt, lt
  Comparator #(.width(7)) comparator_6 (.a(inst[6:0]), .b(7'b1100011), .eq(typeB));  // open: gt, lt
  Comparator #(.width(7)) comparator_7 (.a(inst[6:0]), .b(7'b0110111), .eq(typeLui));  // open: gt, lt
  Comparator #(.width(7)) comparator_8 (.a(inst[6:0]), .b(7'b0010111), .eq(typeAuipc));  // open: gt, lt
  Comparator #(.width(7)) comparator_9 (.a(inst[6:0]), .b(7'b1101111), .eq(typeJ));  // open: gt, lt
  Comparator #(.width(3)) comparator_10 (.a(inst[14:12]), .b(3'b000), .eq(comparator_10_eq));  // open: gt, lt
  not not_1 (not_1_out, BrEq);
  Comparator #(.width(3)) comparator_11 (.a(inst[14:12]), .b(3'b001), .eq(comparator_11_eq));  // open: gt, lt
  Comparator #(.width(3)) comparator_12 (.a(inst[14:12]), .b(3'b100), .eq(comparator_12_eq));  // open: gt, lt
  not not_2 (not_2_out, BrLt);
  Comparator #(.width(3)) comparator_13 (.a(inst[14:12]), .b(3'b101), .eq(comparator_13_eq));  // open: gt, lt
  Comparator #(.width(3)) comparator_14 (.a(inst[14:12]), .b(3'b110), .eq(comparator_14_eq));  // open: gt, lt
  not not_3 (not_3_out, BrLt);
  Comparator #(.width(3)) comparator_15 (.a(inst[14:12]), .b(3'b111), .eq(comparator_15_eq));  // open: gt, lt
  or or_1 (typeI, load, comparator_3_eq, comparator_4_eq);
  or or_2 (typeU, typeLui, typeAuipc);
  and and_1 (and_1_out, BrEq, comparator_10_eq);
  and and_2 (and_2_out, not_1_out, comparator_11_eq);
  and and_3 (and_3_out, BrLt, comparator_12_eq);
  and and_4 (and_4_out, not_2_out, comparator_13_eq);
  and and_5 (and_5_out, BrLt, comparator_14_eq);
  and and_6 (and_6_out, not_3_out, comparator_15_eq);
  or or_3 (or_3_out, and_1_out, and_2_out, and_3_out, and_4_out, and_5_out, and_6_out);
  Comparator #(.width(3)) comparator_16 (.a(inst[14:12]), .b(3'b110), .eq(comparator_16_eq));  // open: gt, lt
  Comparator #(.width(3)) comparator_17 (.a(inst[14:12]), .b(3'b111), .eq(comparator_17_eq));  // open: gt, lt
  Multiplexer #(.enable("false")) multiplexer_1 (.in0(1'b0), .in1(or_3_out), .out(multiplexer_1_out), .sel(typeB));
  Multiplexer #(.enable("false"), .width(3)) multiplexer_2 (
    .in0(3'b000), .in1(3'b001), .out(multiplexer_2_out), .sel(typeI));
  or or_4 (or_4_out, comparator_16_eq, comparator_17_eq);
  or or_5 (ASel, typeB, typeAuipc, typeJ);
  Comparator #(.width(7)) comparator_18 (.a(inst[6:0]), .b(7'b1100111), .eq(typeJalr));  // open: gt, lt
  Multiplexer #(.enable("false"), .width(3)) multiplexer_3 (
    .in0(multiplexer_2_out), .in1(3'b010), .out(multiplexer_3_out), .sel(MemRW));
  Multiplexer #(.enable("false"), .select(3), .width(4)) multiplexer_4 (
    .in0(4'b0000), .in1(4'b0110), .in2(4'b0111), .in4(4'b0011), .in5(4'b0100), .in6(4'b0010), .in7(4'b0001),
    .out(multiplexer_4_out), .sel(inst[14:12]));  // open: in3
  Multiplexer #(.enable("false"), .select(3), .width(4)) multiplexer_5 (
    .in0(4'b1100), .in5(4'b0101), .out(multiplexer_5_out), .sel(inst[14:12]));  // open: in1, in2, in3, in4, in6, in7
  Multiplexer #(.enable("false"), .select(3), .width(4)) multiplexer_6 (
    .in0(4'b1010), .in1(4'b1110), .in3(4'b1011), .out(multiplexer_6_out), .sel(inst[14:12]));  // open: in2, in4, in5, in6, in7
  and and_7 (BrUn, or_4_out, typeB);
  or or_6 (PCSel, typeJalr, typeJ, multiplexer_1_out);
  Multiplexer #(.enable("false"), .width(3)) multiplexer_7 (
    .in0(multiplexer_3_out), .in1(3'b011), .out(multiplexer_7_out), .sel(typeB));
  Multiplexer #(.enable("false"), .select(3), .width(4)) multiplexer_8 (
    .in1(multiplexer_4_out), .in2(multiplexer_5_out), .in4(multiplexer_6_out), .out(multiplexer_8_out),
    .sel(ALUSel0));  // open: in0, in3, in5, in6, in7
  Multiplexer #(.enable("false"), .width(3)) multiplexer_9 (
    .in0(multiplexer_7_out), .in1(3'b100), .out(multiplexer_9_out), .sel(typeU));
  Comparator #(.width(7)) comparator_19 (.a(inst[31:25]), .b({7{1'b0}}), .eq(comparator_19_eq));  // open: gt, lt
  Comparator #(.width(7)) comparator_20 (.a(inst[31:25]), .b(7'b0100000), .eq(comparator_20_eq));  // open: gt, lt
  Comparator #(.width(7)) comparator_21 (.a(inst[31:25]), .b(7'b0000001), .eq(comparator_21_eq));  // open: gt, lt
  Multiplexer #(.enable("false"), .width(4)) multiplexer_10 (
    .in0(4'b0000), .in1(multiplexer_8_out), .out(multiplexer_10_out), .sel(useALU));
  Comparator #(.width(7)) comparator_22 (.a(inst[6:0]), .b(7'b0110011), .eq(comparator_22_eq));  // open: gt, lt
  Comparator #(.width(7)) comparator_23 (.a(inst[6:0]), .b(7'b0010011), .eq(comparator_23_eq));  // open: gt, lt
  Multiplexer #(.enable("false"), .width(3)) multiplexer_11 (
    .in0(multiplexer_9_out), .in1(3'b101), .out(ImmSel), .sel(typeJ));
  and and_8 (ALUSel0[0], hasFunc7, comparator_19_eq);
  and and_9 (ALUSel0[1], hasFunc7, comparator_20_eq);
  and and_10 (ALUSel0[2], hasFunc7, comparator_21_eq);
  Multiplexer #(.enable("false"), .width(4)) multiplexer_12 (
    .in0(multiplexer_10_out), .in1(4'b1101), .out(ALUSel), .sel(or_7_out));
  or or_7 (or_7_out, typeLui, typeCsrrwi);
  or or_8 (useALU, comparator_22_eq, comparator_23_eq);
  Comparator #(.width(7)) comparator_24 (.a(inst[6:0]), .b(7'b1110011), .eq(CSRWen));  // open: gt, lt
  Comparator #(.width(3)) comparator_25 (.a(inst[14:12]), .b(3'b001), .eq(comparator_25_eq));  // open: gt, lt
  Comparator #(.width(3)) comparator_26 (.a(inst[14:12]), .b(3'b101), .eq(comparator_26_eq));  // open: gt, lt
  Multiplexer #(.enable("false")) multiplexer_13 (.in0(1'b0), .in1(1'b1), .out(CSRSel), .sel(typeCsrrwi));
  and and_11 (typeCsrrw, CSRWen, comparator_25_eq);
  and and_12 (typeCsrrwi, CSRWen, comparator_26_eq);
  Comparator #(.width(3)) comparator_27 (.a(inst[14:12]), .b(3'b101), .eq(comparator_27_eq));  // open: gt, lt
  Comparator #(.width(3)) comparator_28 (.a(inst[14:12]), .b(3'b001), .eq(comparator_28_eq));  // open: gt, lt
  Multiplexer #(.enable("false"), .width(2)) multiplexer_14 (
    .in0(2'b00), .in1(2'b01), .out(multiplexer_14_out), .sel(load));
  Multiplexer #(.enable("false"), .width(2)) multiplexer_15 (
    .in0(2'b10), .in1(2'b00), .out(multiplexer_15_out), .sel(b));
  or or_9 (or_9_out, comparator_27_eq, comparator_28_eq);
  or or_10 (RegWEn, CSRWen, typeI, typeR, typeU, typeJ);
  or or_11 (BSel, CSRWen, typeU, typeJ, MemRW, typeB, typeI);
  Multiplexer #(.enable("false"), .width(2)) multiplexer_16 (
    .in0(multiplexer_14_out), .in1(2'b10), .out(multiplexer_16_out), .sel(or_12_out));
  Multiplexer #(.enable("false"), .width(2)) multiplexer_17 (
    .in0(multiplexer_16_out), .in1(2'b11), .out(WBSel), .sel(CSRWen));
  or or_12 (or_12_out, typeJalr, typeJ);
  Comparator #(.width(3)) comparator_29 (.a(inst[14:12]), .b(3'b000), .eq(b));  // open: gt, lt
  Comparator #(.width(3)) comparator_30 (.a(inst[14:12]), .b(3'b001), .eq(h));  // open: gt, lt
  Comparator #(.width(3)) comparator_31 (.a(inst[14:12]), .b(3'b010), .eq(w));  // open: gt, lt
  Multiplexer #(.enable("false"), .width(2)) multiplexer_18 (
    .in0(multiplexer_15_out), .in1(2'b01), .out(loadSel), .sel(h));
  and and_13 (and_13_out, or_9_out, typeI);
  or or_13 (hasFunc7, and_13_out, typeR);

  // Other names for the same wires on the sheet: opcode[6:0] = inst[6:0]; rd[4:0] = inst[11:7];
  //   funct3[2:0] = inst[14:12]; rs1[4:0] = inst[19:15]; rs2[4:0] = inst[24:20]; funct7[6:0] = inst[31:25];
  //   typeCsr = CSRWen; typeS = MemRW

  // Notes on the sheet:
  //   INPUTS to your circuit
  //   DON'T CHANGE THE LOCATIONS OF THE INPUTS AND OUTPUTS!
  //   OUTPUT from your circuit
endmodule
