// Logisim project cpu.circ as structural Verilog: 1 circuit, main circuit cpu
module cpu (
  input  clk,
  input  [31:0] INSTRUCTION,
  input  [31:0] READ_DATA,
  output [31:0] WRITE_ADDRESS,
  output [31:0] PROGRAM_COUNTER,
  output [31:0] ra,
  output [31:0] sp,
  output [31:0] t0,
  output [31:0] t1,
  output [31:0] t2,
  output [31:0] s0,
  output [31:0] s1,
  output [31:0] a0,
  output [31:0] tohost,
  output [3:0] WRITE_ENABLE,
  output [31:0] WRITE_DATA
);

  wire ASel, BrEq, BrLt, BrUn, BSel, CSRSel, CSRWen, MenRW, PCSel, RegWEn;
  wire [1:0] loadSel, WBSel;
  wire [2:0] funct3, ImmSel;
  wire [3:0] ALUSel, multiplexer_7_out;
  wire [6:0] funct7;
  wire [7:0] bit_extender_2_out;
  wire [15:0] bit_extender_4_out;
  wire [24:0] INSTRUCTION_ID;
  wire [31:0] adder_1_out, adder_2_out, bit_extender_1_out, bit_extender_3_out, bit_extender_5_out, Imm,
       imm_gen_1_imm, multiplexer_1_out, multiplexer_2_out, multiplexer_3_out, multiplexer_5_out,
       multiplexer_6_out, PROGRAM_COUNTER_ID, Read_Data_1, SAVE_DATA, WriteData;

  Adder #(.width(32)) adder_1 (.a(PROGRAM_COUNTER), .b(32'h4), .out(adder_1_out));  // open: cin, cout
  Multiplexer #(.enable("false"), .width(32)) multiplexer_1 (
    .in0(adder_1_out), .in1(WRITE_ADDRESS), .out(multiplexer_1_out), .sel(PCSel));
  Multiplexer #(.enable("false"), .width(32)) multiplexer_2 (
    .in0(INSTRUCTION), .in1(32'h13), .out(multiplexer_2_out), .sel(PCSel));
  Register #(.width(32)) PC (.D(multiplexer_1_out), .clk(clk), .Q(PROGRAM_COUNTER));  // open: en, clr
  Register #(.width(32)) register_1 (.D(PROGRAM_COUNTER), .clk(clk), .Q(PROGRAM_COUNTER_ID));  // open: en, clr
  Register #(.width(32)) register_2 (
    .D(multiplexer_2_out), .clk(clk), .Q({funct7, INSTRUCTION_ID[24:15], funct3, INSTRUCTION_ID[11:0]}));  // open: en, clr
  imm_gen imm_gen_1 (
    .inst({funct7, INSTRUCTION_ID[24:15], funct3, INSTRUCTION_ID[11:0]}), .ImmSel(ImmSel), .imm(imm_gen_1_imm));
  Multiplexer #(.enable("false"), .width(32)) multiplexer_3 (
    .in0({32{1'b0}}), .in1(bit_extender_1_out), .out(multiplexer_3_out), .sel(CSRSel));
  assign bit_extender_1_out = {{27{INSTRUCTION_ID[19]}}, INSTRUCTION_ID[19:15]};  // Bit_Extender bit_extender_1
  Multiplexer #(.enable("false"), .width(32)) multiplexer_4 (
    .in0(imm_gen_1_imm), .in1(multiplexer_3_out), .out(Imm), .sel(CSRWen));
  control_logic control_logic_1 (
    .CSRWen(CSRWen), .loadSel(loadSel), .PCSel(PCSel), .RegWEn(RegWEn), .ImmSel(ImmSel), .BrUn(BrUn),
    .ASel(ASel), .BSel(BSel), .ALUSel(ALUSel), .MemRW(MenRW), .WBSel(WBSel), .CSRSel(CSRSel),
    .inst({funct7, INSTRUCTION_ID[24:15], funct3, INSTRUCTION_ID[11:0]}), .BrEq(BrEq), .BrLt(BrLt));
  regfile regfile_1 (
    .rs1(INSTRUCTION_ID[19:15]), .rs2(INSTRUCTION_ID[24:20]), .rd(INSTRUCTION_ID[11:7]),
    .Write_Data(WriteData), .RegWEn(RegWEn), .clk(clk), .ra(ra), .sp(sp), .t0(t0), .t1(t1), .t2(t2), .s0(s0),
    .s1(s1), .a0(a0), .Read_Data_1(Read_Data_1), .Read_Data_2(WRITE_DATA));
  branch_comp branch_comp_1 (.rs1(Read_Data_1), .rs2(WRITE_DATA), .BrUn(BrUn), .BrEq(BrEq), .BrLt(BrLt));
  Multiplexer #(.enable("false"), .width(32)) multiplexer_5 (
    .in0(Read_Data_1), .in1(PROGRAM_COUNTER_ID), .out(multiplexer_5_out), .sel(ASel));
  Multiplexer #(.enable("false"), .width(32)) multiplexer_6 (
    .in0(WRITE_DATA), .in1(Imm), .out(multiplexer_6_out), .sel(BSel));
  csr csr_1 (.CSR_address(12'h51e), .CSR_din(WRITE_ADDRESS), .CSR_WE(CSRWen), .clk(clk), .tohost(tohost));
  alu alu_1 (.Result(WRITE_ADDRESS), .A(multiplexer_5_out), .B(multiplexer_6_out), .ALUSel(ALUSel));
  Adder #(.width(32)) adder_2 (.a(PROGRAM_COUNTER_ID), .b(32'h4), .out(adder_2_out));  // open: cin, cout
  Multiplexer #(.enable("false"), .select(2), .width(4)) multiplexer_7 (
    .in0(4'b0001), .in1(4'b0011), .in2(4'b1111), .out(multiplexer_7_out), .sel(loadSel));  // open: in3
  Multiplexer #(.enable("false"), .select(2), .width(32)) multiplexer_8 (
    .in0(WRITE_ADDRESS), .in1(SAVE_DATA), .in2(adder_2_out), .in3(tohost), .out(WriteData), .sel(WBSel));
  Bit_Extender #(.in_width(32), .out_width(8), .\type ("zero")) bit_extender_2 (
    .in(READ_DATA), .out(bit_extender_2_out));
  assign bit_extender_3_out = {{24{bit_extender_2_out[7]}}, bit_extender_2_out};  // Bit_Extender bit_extender_3
  Bit_Extender #(.in_width(32), .\type ("zero")) bit_extender_4 (.in(READ_DATA), .out(bit_extender_4_out));
  assign bit_extender_5_out = {{16{bit_extender_4_out[15]}}, bit_extender_4_out};  // Bit_Extender bit_extender_5
  Multiplexer #(.enable("false"), .width(4)) multiplexer_9 (
    .in0(4'b0000), .in1(multiplexer_7_out), .out(WRITE_ENABLE), .sel(MenRW));
  Multiplexer #(.enable("false"), .select(2), .width(32)) multiplexer_10 (
    .in0(bit_extender_3_out), .in1(bit_extender_5_out), .in2(READ_DATA), .out(SAVE_DATA), .sel(loadSel));  // open: in3

  // Other names for the same wires on the sheet: ALU_Res[31:0] = WRITE_ADDRESS; opcode[6:0] = INSTRUCTION_ID[6:0];
  //   rd[4:0] = INSTRUCTION_ID[11:7]; INSTRUCTION_ID (some bits) = {funct7, funct3}; rs1[4:0] = INSTRUCTION_ID[19:15];
  //   rs2[4:0] = INSTRUCTION_ID[24:20]; Read_Data_2[31:0] = WRITE_DATA

  // Notes on the sheet:
  //   Output to IMEM
  //   IMEM (do **NOT** move this)
  //   Inputs from IMEM
  //   It is OK to move the PC, RegFile, ALU, MEM, Branch Comp, Imm Gen, and Control Logic to wherever is most convenient for you when constructing your CPU, and to delete this text
  //   Inputs/Outputs for testing. Do **NOT** move these.
  //   Outputs To DMEM
  //   DMEM (do **NOT** move this)
  //   Inputs From DMEM
endmodule
