// Logisim project regfile.circ as structural Verilog: 1 circuit, main circuit regfile
module regfile (
  input  [4:0] rs1,
  input  [4:0] rs2,
  input  [4:0] rd,
  input  [31:0] Write_Data,
  input  RegWEn,
  input  clk,
  output [31:0] ra,
  output [31:0] sp,
  output [31:0] t0,
  output [31:0] t1,
  output [31:0] t2,
  output [31:0] s0,
  output [31:0] s1,
  output [31:0] a0,
  output [31:0] Read_Data_1,
  output [31:0] Read_Data_2
);

  wire a0_we, a1_we, a2_we, a3_we, a4_we, a5_we, a6_we, a7_we, gp_we, ra_we, s0_we, s1_we, s2_we, s3_we,
       s4_we, s5_we, s6_we, s7_we, s8_we, s9_we, s10_we, s11_we, sp_we, t0_we, t1_we, t2_we, t3_we, t4_we,
       t5_we, t6_we, tp_we, x0_we;
  wire [31:0] a0_w, a1, a1_w, a2, a2_w, a3, a3_w, a4, a4_w, a5, a5_w, a6, a6_w, a7, a7_w, gp, gp_w, ra_w,
       s0_w, s1_w, s2, s2_w, s3, s3_w, s4, s4_w, s5, s5_w, s6, s6_w, s7, s7_w, s8, s8_w, s9, s9_w, s10,
       s10_w, s11, s11_w, sp_w, t0_w, t1_w, t2_w, t3, t3_w, t4, t4_w, t5, t5_w, t6, t6_w, tp, tp_w, x0, x0_w;

  Register #(.width(32)) register_1 (.Q(x0));  // open: D, en, clk, clr
  Register #(.width(32)) register_2 (.D(ra_w), .en(ra_we), .clk(clk), .Q(ra));  // open: clr
  Register #(.width(32)) register_3 (.D(sp_w), .en(sp_we), .clk(clk), .Q(sp));  // open: clr
  Register #(.width(32)) register_4 (.D(gp_w), .en(gp_we), .clk(clk), .Q(gp));  // open: clr
  Register #(.width(32)) register_5 (.D(tp_w), .en(tp_we), .clk(clk), .Q(tp));  // open: clr
  Register #(.width(32)) register_6 (.D(t0_w), .en(t0_we), .clk(clk), .Q(t0));  // open: clr
  Multiplexer #(.enable("false"), .select(5), .width(32)) multiplexer_1 (
    .in0(x0), .in1(ra), .in2(sp), .in3(gp), .in4(tp), .in5(t0), .in6(t1), .in7(t2), .in8(s0), .in9(s1),
    .in10(a0), .in11(a1), .in12(a2), .in13(a3), .in14(a4), .in15(a5), .in16(a6), .in17(a7), .in18(s2),
    .in19(s3), .in20(s4), .in21(s5), .in22(s6), .in23(s7), .in24(s8), .in25(s9), .in26(s10), .in27(s11),
    .in28(t3), .in29(t4), .in30(t5), .in31(t6), .out(Read_Data_1), .sel(rs1));
  Register #(.width(32)) register_7 (.D(t1_w), .en(t1_we), .clk(clk), .Q(t1));  // open: clr
  Register #(.width(32)) register_8 (.D(t2_w), .en(t2_we), .clk(clk), .Q(t2));  // open: clr
  Register #(.width(32)) register_9 (.D(s0_w), .en(s0_we), .clk(clk), .Q(s0));  // open: clr
  Register #(.width(32)) register_10 (.D(s1_w), .en(s1_we), .clk(clk), .Q(s1));  // open: clr
  Register #(.width(32)) register_11 (.D(a0_w), .en(a0_we), .clk(clk), .Q(a0));  // open: clr
  Register #(.width(32)) register_12 (.D(a1_w), .en(a1_we), .clk(clk), .Q(a1));  // open: clr
  Register #(.width(32)) register_13 (.D(a2_w), .en(a2_we), .clk(clk), .Q(a2));  // open: clr
  Register #(.width(32)) register_14 (.D(a3_w), .en(a3_we), .clk(clk), .Q(a3));  // open: clr
  Register #(.width(32)) register_15 (.D(a4_w), .en(a4_we), .clk(clk), .Q(a4));  // open: clr
  Register #(.width(32)) register_16 (.D(a5_w), .en(a5_we), .clk(clk), .Q(a5));  // open: clr
  Register #(.width(32)) register_17 (.D(a6_w), .en(a6_we), .clk(clk), .Q(a6));  // open: clr
  Register #(.width(32)) register_18 (.D(a7_w), .en(a7_we), .clk(clk), .Q(a7));  // open: clr
  Multiplexer #(.enable("false"), .select(5), .width(32)) multiplexer_2 (
    .in0(x0), .in1(ra), .in2(sp), .in3(gp), .in4(tp), .in5(t0), .in6(t1), .in7(t2), .in8(s0), .in9(s1),
    .in10(a0), .in11(a1), .in12(a2), .in13(a3), .in14(a4), .in15(a5), .in16(a6), .in17(a7), .in18(s2),
    .in19(s3), .in20(s4), .in21(s5), .in22(s6), .in23(s7), .in24(s8), .in25(s9), .in26(s10), .in27(s11),
    .in28(t3), .in29(t4), .in30(t5), .in31(t6), .out(Read_Data_2), .sel(rs2));
  Register #(.width(32)) register_19 (.D(s2_w), .en(s2_we), .clk(clk), .Q(s2));  // open: clr
  Register #(.width(32)) register_20 (.D(s3_w), .en(s3_we), .clk(clk), .Q(s3));  // open: clr
  Register #(.width(32)) register_21 (.D(s4_w), .en(s4_we), .clk(clk), .Q(s4));  // open: clr
  Register #(.width(32)) register_22 (.D(s5_w), .en(s5_we), .clk(clk), .Q(s5));  // open: clr
  Register #(.width(32)) register_23 (.D(s6_w), .en(s6_we), .clk(clk), .Q(s6));  // open: clr
  Register #(.width(32)) register_24 (.D(s7_w), .en(s7_we), .clk(clk), .Q(s7));  // open: clr
  Demultiplexer #(.enable("false"), .select(5), .width(32)) demultiplexer_1 (
    .out0(x0_w), .out1(ra_w), .out2(sp_w), .out3(gp_w), .out4(tp_w), .out5(t0_w), .out6(t1_w), .out7(t2_w),
    .out8(s0_w), .out9(s1_w), .out10(a0_w), .out11(a1_w), .out12(a2_w), .out13(a3_w), .out14(a4_w),
    .out15(a5_w), .out16(a6_w), .out17(a7_w), .out18(s2_w), .out19(s3_w), .out20(s4_w), .out21(s5_w),
    .out22(s6_w), .out23(s7_w), .out24(s8_w), .out25(s9_w), .out26(s10_w), .out27(s11_w), .out28(t3_w),
    .out29(t4_w), .out30(t5_w), .out31(t6_w), .in(Write_Data), .sel(rd));
  Register #(.width(32)) register_25 (.D(s8_w), .en(s8_we), .clk(clk), .Q(s8));  // open: clr
  Register #(.width(32)) register_26 (.D(s9_w), .en(s9_we), .clk(clk), .Q(s9));  // open: clr
  Register #(.width(32)) register_27 (.D(s10_w), .en(s10_we), .clk(clk), .Q(s10));  // open: clr
  Register #(.width(32)) register_28 (.D(s11_w), .en(s11_we), .clk(clk), .Q(s11));  // open: clr
  Register #(.width(32)) register_29 (.D(t3_w), .en(t3_we), .clk(clk), .Q(t3));  // open: clr
  Register #(.width(32)) register_30 (.D(t4_w), .en(t4_we), .clk(clk), .Q(t4));  // open: clr
  Register #(.width(32)) register_31 (.D(t5_w), .en(t5_we), .clk(clk), .Q(t5));  // open: clr
  Register #(.width(32)) register_32 (.D(t6_w), .en(t6_we), .clk(clk), .Q(t6));  // open: clr
  Demultiplexer #(.enable("false"), .select(5)) demultiplexer_2 (
    .out0(x0_we), .out1(ra_we), .out2(sp_we), .out3(gp_we), .out4(tp_we), .out5(t0_we), .out6(t1_we),
    .out7(t2_we), .out8(s0_we), .out9(s1_we), .out10(a0_we), .out11(a1_we), .out12(a2_we), .out13(a3_we),
    .out14(a4_we), .out15(a5_we), .out16(a6_we), .out17(a7_we), .out18(s2_we), .out19(s3_we), .out20(s4_we),
    .out21(s5_we), .out22(s6_we), .out23(s7_we), .out24(s8_we), .out25(s9_we), .out26(s10_we),
    .out27(s11_we), .out28(t3_we), .out29(t4_we), .out30(t5_we), .out31(t6_we), .in(RegWEn), .sel(rd));

  // Other names for the same wires on the sheet: read_data1[31:0] = Read_Data_1; read_data2[31:0] = Read_Data_2;
  //   read_reg1[4:0] = rs1; read_reg2[4:0] = rs2; write_en = RegWEn; write_reg[4:0] = rd

  // Notes on the sheet:
  //   INPUTS to your circuit
  //   DON'T CHANGE THE LOCATIONS OF THE INPUTS AND OUTPUTS!
  //   These are DEBUG/TEST outputs from your circuit.
  //   OUTPUTS from your circuit
endmodule
